// Logisim project LC-2200-16.circ as structural Verilog: 3 circuits, main circuit main
module main (
  input  LdA,
  input  LdB,
  input  LdPC,
  input  WrREG,
  input  [1:0] func,
  input  [3:0] regno,
  input  DrPC,
  input  DrALU,
  input  DrREG
);

  wire CLK;
  wire [15:0] A_q, alux16_1_output, B_q, controlled_buffer_1_out, PC_q, register_array_1_din_2;

  Clock clock_1 (.out(CLK));
  Counter #(.width(16), .max('hffff)) PC (
    .load(LdPC), .D(controlled_buffer_1_out), .Q(PC_q), .clk(CLK));  // open: count, carry, clr
  assign controlled_buffer_1_out = DrPC ? PC_q : 16'bz;  // Controlled_Buffer controlled_buffer_1
  Register #(.width(16)) A (.D(controlled_buffer_1_out), .en(LdA), .Q(A_q), .clk(CLK));  // open: clr
  ALUx16 alux16_1 (.func(func), .A(A_q), .B(B_q), .\output (alux16_1_output));
  assign controlled_buffer_1_out = DrALU ? alux16_1_output : 16'bz;  // Controlled_Buffer controlled_buffer_2
  Register #(.width(16)) B (.D(controlled_buffer_1_out), .en(LdB), .Q(B_q), .clk(CLK));  // open: clr
  register_array register_array_1 (
    .WrREG(WrREG), .regno(regno), .Din(controlled_buffer_1_out), .Din_2(register_array_1_din_2));
  assign controlled_buffer_1_out = DrREG ? register_array_1_din_2 : 16'bz;  // Controlled_Buffer controlled_buffer_3
  RAM #(.addrWidth(16), .dataWidth(16)) ram_1 ();  // open: addr, data, sel, clk, ld, clr
endmodule

module ALUx16 (
  input  [15:0] A,
  input  [15:0] B,
  input  [1:0] func,
  output [15:0] \output 
);

  wire [15:0] adder_1_out, adder_2_out, demultiplexer_1_out0, demultiplexer_1_out1, demultiplexer_1_out2,
       demultiplexer_1_out3, demultiplexer_2_out0, demultiplexer_2_out1, demultiplexer_2_out2,
       demultiplexer_2_out3, nand_1_out, subtractor_1_out;

  Adder #(.width(16)) adder_1 (
    .a(demultiplexer_1_out0), .b(demultiplexer_2_out0), .out(adder_1_out));  // open: cin, cout
  Demultiplexer #(.select(2), .width(16)) demultiplexer_1 (
    .out0(demultiplexer_1_out0), .out1(demultiplexer_1_out1), .out2(demultiplexer_1_out2),
    .out3(demultiplexer_1_out3), .in(A), .sel(func));  // open: en
  assign nand_1_out = ~(demultiplexer_1_out1 & demultiplexer_2_out1);  // NAND_Gate nand_1, 16 bits wide
  Subtractor #(.width(16)) subtractor_1 (
    .a(demultiplexer_1_out2), .b(demultiplexer_2_out2), .out(subtractor_1_out));  // open: bin, bout
  Multiplexer #(.select(2), .width(16)) multiplexer_1 (
    .in0(adder_1_out), .in1(nand_1_out), .in2(subtractor_1_out), .in3(adder_2_out), .out(\output ), .sel(func));  // open: en
  Demultiplexer #(.select(2), .width(16)) demultiplexer_2 (
    .out0(demultiplexer_2_out0), .out1(demultiplexer_2_out1), .out2(demultiplexer_2_out2),
    .out3(demultiplexer_2_out3), .in(B), .sel(func));  // open: en
  Adder #(.width(16)) adder_2 (.a(demultiplexer_1_out3), .b(16'h1), .out(adder_2_out));  // open: cin, cout
  // also tied to GND on the sheet: {demultiplexer_2_out3[0], demultiplexer_2_out3[1], demultiplexer_2_out3[2], demultiplexer_2_out3[3], demultiplexer_2_out3[4], demultiplexer_2_out3[5], demultiplexer_2_out3[6], demultiplexer_2_out3[7], demultiplexer_2_out3[8], demultiplexer_2_out3[9], demultiplexer_2_out3[10], demultiplexer_2_out3[11], demultiplexer_2_out3[12], demultiplexer_2_out3[13], demultiplexer_2_out3[14], demultiplexer_2_out3[15]}
endmodule

module register_array (
  input  [15:0] Din,
  input  WrREG,
  input  [3:0] regno,
  output [15:0] Din_2
);
endmodule
